# Fritzing sketch diagramaA (saved by Fritzing 0.8.3b)
breadboards: 1

parts:
  Parte1 = Arduino Uno (Rev3)
  LED1 = LED - 5mm [color="Red (633nm)" package="5 mm [THT]"]
  LED2 = LED - 5mm [color="Green (570nm)" package="5 mm [THT]"]
  LED3 = LED - 5mm [color="Green (570nm)" package="5 mm [THT]"]
  LED4 = LED - 5mm [color="Green (570nm)" package="5 mm [THT]"]
  S1 = Pushbutton [package="[THT]"]
  R1 = Resistor [tolerance=±5% resistance=100k package=THT]

nets:
  N1: Parte1.GND, LED1.cathode, LED2.cathode, LED3.cathode, LED4.cathode, R1.Pin_0
  N2: Parte1.D8, LED3.anode
  N3: Parte1.D12/MISO, LED2.anode
  N4: Parte1.D13/SCK, LED1.anode
  N5: Parte1.D3_PWM, S1.Pin_1, S1.Pin_2, R1.Pin_1
  N6: Parte1.D7, LED4.anode
  N7: Parte1.5V, S1.Pin_3, S1.Pin_4
