# Fritzing sketch diagramaB (saved by Fritzing 0.9.0b)
breadboards: 1

parts:
  Parte1 = Arduino Uno (Rev3)
  LED2 = LED - 3mm [color="Green (555nm)" package="3 mm [THT]"]
  LED3 = LED - 3mm [color="Green (555nm)" package="3 mm [THT]"]
  LED4 = LED - 3mm [color="Green (555nm)" package="3 mm [THT]"]
  LED5 = LED - 3mm [color="Red (633nm)" package="3 mm [THT]"]
  R1 = Resistor [package="2010 [SMD]"]
  R2 = Resistor [package="2010 [SMD]"]
  R3 = Resistor [package="2010 [SMD]"]
  R4 = Resistor [package="2010 [SMD]"]
  S1 = Pushbutton [package="[THT]"]
  R8 = Resistor [tolerance=±5% resistance=10k package="0805 [SMD]"]
  J2 = Piezo Speaker

nets:
  N1: Parte1.D9_PWM, LED3.anode
  N2: Parte1.D10_PWM/SS, LED4.anode
  N3: Parte1.D11_PWM/MOSI, LED5.anode
  N4: Parte1.D3_PWM, S1.Pin_1, S1.Pin_2, R8.Pin_1
  N5: Parte1.D6_PWM, LED2.anode
  N6: Parte1.5V, S1.Pin_3, S1.Pin_4
  N7: LED2.cathode, R4.Pin_0
  N8: LED3.cathode, R3.Pin_0
  N9: LED4.cathode, R2.Pin_0
  N10: LED5.cathode, R1.Pin_0
  N11: R1.Pin_1, R2.Pin_1, R3.Pin_1, R4.Pin_1, R8.Pin_0, J2.pin1
